# Fritzing sketch DC_Sensor_Fritzing_Schematic (saved by Fritzing 0.8.5b)
breadboards: 1

parts:
  R1 = Resistor [tolerance=±5% resistance=15k package=THT]
  Part1 = Arduino Uno (Rev3)

nets:
  N1: R1.Pin_0, Part1.A0
  N2: R1.Pin_1, Part1.5V
