# Fritzing sketch Fritzing_Raw (saved by Fritzing 0.8.5b)
breadboards: 1

parts:
  U1 = 555 Timer [package="DIP8 [THT]"]
  C6 = Ceramic Capacitor [capacitance="100 nF" package="0603 [SMD, multilayer]"]
  C3 = Capacitor [package=cap-pth-small2]
  R3 = Resistor [tolerance=±1% resistance=56k package=THT]
  Part1 = Arduino Uno (Rev3)

nets:
  N1: U1.Ground, C6.0, C3.2, Part1.GND
  N2: U1.Trigger, U1.Threshold, C3.1, R3.Pin_1
  N3: U1.Output, Part1.D3_PWM
  N4: U1.Reset, U1.Vcc_Supply_Voltage, Part1.5V
  N5: U1.Discharge, R3.Pin_0

notes:
  56kOhm
  <module fritzingVersion="0.8.5b.12.16.8b2c">
  <boundingRects>
  <boundingRect rect="301.154 160.223 42.75 7.74" name="PCB View"/>
  <boundingRect rect="373.25 97.6368 9.9999 40.0687" name="Breadboard View"/>
  <boundingRect rect="997.166 514.555 15.6988 81.4687" name="Schematic View"/>
  </boundingRects>
  <instances>
  <instance moduleIdRef="5BandResistorModuleID" modelIndex="2159" path="/Applications/Fritzing.app/Contents/MacOS/pdb/core/resistor_5band.fzp">
  <property value="±1%" name="tolerance"/>
  <property value="56k" name="resistance"/>
  <property value="400 mil" name="pin spacing"/>
  <property value="" name="power"/>
  <title>R2</title>
  <views>
  <breadboardView layer="breadboard">
  <geometry x="358.25" y="112.706" z="2.00002">
  <transform m31="24.9997" m21="-1" m32="-14.9999" m11="2.22045e-16" m22="2.22045e-16" m33="1" m12="1" m23="0" m13="0"/>
  </geometry>
  <connectors>
  <connector connectorId="connector0" layer="breadboard">
  <geometry x="1.81873" y="4.29871"/>
  <leg>
  <point x="0" y="0"/>
  <bezier/>
  <point x="-0.0690548" y="1.42109e-14"/>
  <bezier/>
  </leg>
  <connects/>
  </connector>
  <connector connectorId="connector1" layer="breadboard">
  <geometry x="37.2496" y="4.29871"/>
  <leg>
  <point x="0" y="0"/>
  <bezier/>
  <point x="0.499995" y="1.42109e-14"/>
  <bezier/>
  </leg>
  <connects/>
  </connector>
  </connectors>
  </breadboardView>
  <pcbView layer="copper0">
  <geometry x="301.154" y="160.223" z="5.50001"/>
  <titleGeometry x="343.904" xOffset="42.75" y="153.223" yOffset="-7" z="12.5002" fontSize="5" visible="true" textColor="#000000">
  <displayKey key=""/>
  </titleGeometry>
  <connectors>
  <connector connectorId="connector0" layer="copper0">
  <geometry x="0" y="0"/>
  <connects/>
  </connector>
  <connector connectorId="connector1" layer="copper0">
  <geometry x="0" y="0"/>
  <connects/>
  </connector>
  </connectors>
  </pcbView>
  <schematicView layer="schematic">
  <geometry x="997.166" y="514.555" z="2.50001"/>
  <titleGeometry x="1012.87" xOffset="15.6988" y="489.555" yOffset="-25" z="6.50019" fontSize="9" visible="true" textColor="#000000">
  <displayKey key=""/>
  <displayKey key="part number"/>
  <displayKey key="resistance"/>
  <displayKey key="power"/>
  </titleGeometry>
  <connectors>
  <connector connectorId="connector0" layer="schematic">
  <geometry x="0" y="0"/>
  <connects/>
  </connector>
  <connector connectorId="connector1" layer="schematic">
  <geometry x="0" y="0"/>
  <connects/>
  </connector>
  </connectors>
  </schematicView>
  </views>
  </instance>
  </instances>
  </module>
  Note: decrease this resistor value to increase the sensor's sensitivity
  These are the sensor probes
  The bage capacitor will be 680nF (this is sometimes listed as 0.68uF)
  The blue capacitor will be 0.01 uF
